// Digital circuit control_bomba.dig as structural Verilog
module control_bomba (
  input  tanqueH,
  input  tanqueL,
  input  cisternaOK,
  input  cisternaL,
  output bomba
);

  wire and_1_out, or_1_out;

  and and_1 (and_1_out, ~tanqueL, cisternaOK);  // And
  or or_1 (or_1_out, tanqueH, ~cisternaL);  // Or
  RS_FF_AS rs_ff_as_1 (.S(and_1_out), .R(or_1_out), .Q(bomba));  // open: nQ
endmodule
