// Digital circuit unidad_aritmetica_logica.dig as structural Verilog
module unidad_aritmetica_logica (
  input  [15:0] A,
  input  [15:0] B,
  input  invB,
  input  logica,
  input  \and ,
  output [15:0] R
);

  wire [15:0] B_t, not_1_out, or_1_out;

  assign not_1_out = ~B;  // Not not_1, 16 bits wide
  Multiplexer #(.Bits(16)) multiplexer_1 (.sel(invB), .in_0(B), .in_1(not_1_out), .out(B_t));
  assign or_1_out = A | B_t;  // Or or_1, 16 bits wide
  Multiplexer #(.Bits(16)) multiplexer_2 (.sel(logica), .in_0({16{1'b0}}), .in_1(or_1_out), .out(R));
endmodule
